// Logisim project D_FlipFlop.circ as structural Verilog: 1 circuit, main circuit D_FlipFlop
// D Flip-Flop — CPU Register Bit
module D_FlipFlop (
  input  D,
  input  CLK,
  output Q
);

  D_Flip_Flop #(.trigger("high")) d_ff_1 (.D(D), .clk(CLK), .Q(Q));  // open: Qn, preset, reset
endmodule
