// Logisim project Mod60_Counter.circ as structural Verilog: 1 circuit, main circuit Mod60_Counter
// Mod-60 Counter — Digital Clock Seconds
module Mod60_Counter (
  input  CLK,
  output [5:0] COUNT_5_0
);

  // Counter #(.width(6), .max('h3B)) COUNT_00_59: pin names not known; wires that end beside it: CLK, COUNT_5_0
endmodule
