// Logisim project SIPO_Register.circ as structural Verilog: 1 circuit, main circuit SIPO_Register
// 4-bit SIPO Shift Register
module SIPO_Register (
  input  SERIAL_IN,
  input  CLK,
  output Q0,
  output Q1,
  output Q2,
  output Q3
);

  // D_Flip_Flop #(.trigger("high")) FF0: pin names not known; wires that end beside it: SERIAL_IN, CLK, Q0
  // D_Flip_Flop #(.trigger("high")) FF1: pin names not known; wires that end beside it: Q0, CLK, Q1
  // D_Flip_Flop #(.trigger("high")) FF2: pin names not known; wires that end beside it: Q1, CLK, Q2
  D_Flip_Flop #(.trigger("high")) FF3 (.D(Q2), .clk(CLK), .Q(Q3));  // open: Qn, preset, reset
endmodule
